# Fritzing sketch TeaMachineSchematic (saved by Fritzing 0.9.2b)
breadboards: 1

parts:
  Part2 = Arduino Uno (Rev3)
  U1 = RELAY [package=relay-g5q]
  U2 = RELAY [package=relay-g5q]
  U3 = mystery part, 3 pins [chip_label="Flow Meter"]
  S1 = Pushbutton [package="[THT]"]
  S2 = Pushbutton [package="[THT]"]
  S3 = Pushbutton [package="[THT]"]
  R1 = Resistor [tolerance=±5% resistance=220 package=THT]
  L1 = Inductor [package="400 mil [THT]"]

nets:
  GND: Part2.GND, U1.COIL2, U1.NC, U2.COIL2, U2.NC, U3.pin2, S1.Pin_3, S1.Pin_4, S2.Pin_3, S2.Pin_4, S3.Pin_3, S3.Pin_4, R1.Pin_1, L1.pin_1
  N1: Part2.D2, U3.pin1
  N2: Part2.D3_PWM, U2.COIL1
  N3: Part2.D4, U1.COIL1
  N4: Part2.D5_PWM, S3.Pin_1, S3.Pin_2
  N5: Part2.D6_PWM, S2.Pin_1, S2.Pin_2
  N6: Part2.D7, S1.Pin_1, S1.Pin_2
  5V: Part2.5V, U3.pin3
  N7: U1.MAIN, R1.Pin_0
  240V: U1.NO, U2.NO
  N8: U2.MAIN, L1.pin_0

// code stored in the sketch: TeaMachineCode.ino
// Draft of code to be  used in the tea machine

// Analog Inputs
int TempAdj = 18; // This is connected to the TempAdj Pot
int VarTempAdj; // Current Temp Setting (NOT THE ACTUAL TEMP)

// Not Really Analog
// THIS SUBSECTION IS SET FOR THE DS18B20 SENSOR
int ReadTemp = 7; // Temperature read from the sensor
int VarReadTemp; // Variable for ReadTemp

// Digital Inputs
int Small = 8; // the smallest cup size
int VarSmall; 

int Med = 9; // Medium cup size
int VarMed; 

int Large = 10; // Large cup size
int VarLarge;

int FlowRate = 6; // The output from the flow rate measuring thing
int VarFlowRate; // 1925 pulses per litre with 1.2mm nozzle

void setup () {
  Serial.begin(9600);
  // Analog Assignment Section


  // Digital Assignment Section
  pinMode(Small, INPUT);
  pinMode(Med, INPUT);
  PinMode(Large, INPUT);
  
}

void loop() {
  // ### Analog Input Section ###

  VarTempAdj = analogRead(TempAjd);
  Serial.println(VarTempAdj);

  // Read Current Temperature
  VarReadTemp = analogRead(ReadTemp);
  Serial.println(VarReadTemp);

  // ### Digital Input Section ###


  VarSmall = digitalRead(Small); // Pin 8
  Serial.println(VarSmall);

  VarMed = digitalRead(Med); // Pin 9
  Serial.println(VarMed);
  
  Varlarge = digitalRead(Large); // Pin 10
  Serial.println(VarLarge);

  // End Preliminary Setup  


  

}
